# Fritzing sketch buttons_sketch (saved by Fritzing 0.9.3b)
breadboards: 1

parts:
  Raspberry_Pi_1 = Raspberry Pi 3 [part_number=RPI-3-V1.2]
  S1 = Pushbutton [package="[SMD]"]
  S2 = Pushbutton [package="[SMD]"]
  R1 = Resistor [tolerance=±5% resistance=220 package=THT]
  R2 = Resistor [tolerance=±5% resistance=220 package=THT]

nets:
  N1: Raspberry_Pi_1.GND, R1.Pin_0, R2.Pin_0
  N2: S1.Pin_1, S1.Pin_2, R1.Pin_1
  N3: S2.Pin_3, S2.Pin_4, R2.Pin_1
