# Fritzing sketch speakers_sketch (saved by Fritzing 0.9.3b)
perfboards: 1

parts:
  Raspberry_Pi_1 = Raspberry Pi 3 [part_number=RPI-3-V1.2]
  J1 = female pin header, 3 pins [form="♀ (female)"]  # not connected
  J2 = female pin header, 2 pins [form="♀ (female)"]
  J3 = female pin header, 2 pins [form="♀ (female)"]
  J4 = female pin header, 2 pins [form="♀ (female)"]
  IC1 = IC, DIP package, 16 pins [chip_label=PAM8403]  # not connected
  SP1 = SPEAKER [package=pcb_mount_speaker]
  SP2 = SPEAKER [package=pcb_mount_speaker]

nets:
  N1: Raspberry_Pi_1.GND, J2.pin1
  N2: Raspberry_Pi_1.5V, J2.pin2
  N3: J3.pin1, SP2.+
  N4: J3.pin2, SP2.-
  N5: J4.pin1, SP1.-
  N6: J4.pin2, SP1.+

notes:
  +
  -
  R
  L
  5V
